# Fritzing sketch esp12-sm50-pinheaders (saved by Fritzing 0.9.3b)
circuit board: 5.74854cm x 3.03092cm
breadboards: 1

parts:
  RST = Pushbutton [package=THT]
  R7 = Resistor [tolerance=±5% resistance=470 package=THT]
  C3 = Electrolytic Capacitor [capacitance=2.2µF package="100 mil [THT, electrolytic]"]
  R5 = Resistor [tolerance=±5% resistance=10k package=THT]
  program = male pin header, 6 pins [form="♂ (male)"]
  R3 = Resistor [tolerance=±5% resistance=10k package=THT]
  P1 = male pin header, 6 pins [form="♂ (male)"]
  PRG = Pushbutton [package=THT]
  R2 = Resistor [tolerance=±5% resistance=10k package=THT]
  R6 = Resistor [tolerance=±5% resistance=10k package=THT]
  C1 = Ceramic Capacitor [capacitance=100nF package="100 mil [THT, multilayer]"]
  IC4 = ESP8266-12e_tht [part_number=ESP8266-12E]
  R1 = Resistor [tolerance=±5% resistance=10k package=THT]
  LED1 = LED - 5mm [color="Green (565nm)" package="5 mm [THT]"]
  R4 = Resistor [tolerance=±5% resistance=10k package=THT]
  U1 = Voltage Regulator - 3.3V [package="TO220 [THT]"]

nets:
  GND: RST.leg0, C3.-, R5.Pin_0, program.pin6, P1.pin1, P1.pin4, PRG.leg0, C1.0, IC4.GND, U1.GND
  N1: RST.leg1, IC4.REST, R1.Pin_0
  N2: R7.Pin_0, P1.pin5
  N3: R7.Pin_1, LED1.cathode
  5V: C3.+, P1.pin6, LED1.anode, U1.input_voltage
  N4: R5.Pin_1, IC4.GPIO_15
  N5: program.pin2, IC4.GPIO_1/TXD
  N6: program.pin3, P1.pin2, R6.Pin_1, IC4.GPIO_3/RXD
  3.3V: R3.Pin_0, R2.Pin_1, R6.Pin_0, C1.1, IC4.VCC, R1.Pin_1, R4.Pin_0, U1.output_voltage
  N7: R3.Pin_1, PRG.leg1, IC4.GPIO_0
  N8: R2.Pin_0, IC4.CH_PD
  N9: IC4.GPIO_2, R4.Pin_1

notes:
  Smartmeter P1 lezer, A
  DIEL002-RevA
  mei 2019
  DATA
  GND
  REQ
  Vcc

custom parts:
  ESP8266-12e_tht: These are the first series of modules made with the ESP8266 by the third-party manufacturer AI-Thinker and remain the most widely available. They are collectively referred to as "ESP-xx modules" and to form a workable development system require additional components, especially a serial TTL-to-USB adapter (sometimes called a USB-to-UART bridge) and an external 3.3V power supply. The pcb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
  Voltage Regulator - 3.3V: 3.3V DC Voltage Regulator
